// Logisim project Digital clock.circ as structural Verilog: 6 circuits, main circuit main
module main (
);

  wire and_1_out, and_2_out, and_3_out, and_4_out, and_5_out, and_6_out, clock_1_out, mod1_1_q1, mod1_1_q2,
       mod1_1_q3, mod1_1_q4, mod2_1_q1, mod2_1_q2, mod_6_1_q1, mod_6_1_q2, mod_6_1_q3, mod_6_1_q4,
       mod_6_2_q1, mod_6_2_q2, mod_6_2_q3, mod_6_2_q4, mod_10_1_q1, mod_10_1_q2, mod_10_1_q3, mod_10_1_q4,
       mod_10_2_q1, mod_10_2_q2, mod_10_2_q3, mod_10_2_q4, n7_segment_1_a, n7_segment_1_b, n7_segment_1_c,
       n7_segment_1_d, n7_segment_1_e, n7_segment_1_f, n7_segment_1_g, n7_segment_2_a, n7_segment_2_b,
       n7_segment_2_c, n7_segment_2_d, n7_segment_2_e, n7_segment_2_f, n7_segment_2_g, n7_segment_3_a,
       n7_segment_3_b, n7_segment_3_c, n7_segment_3_d, n7_segment_3_e, n7_segment_3_f, n7_segment_3_g,
       n7_segment_4_a, n7_segment_4_b, n7_segment_4_c, n7_segment_4_d, n7_segment_4_e, n7_segment_4_f,
       n7_segment_4_g, n7_segment_5_a, n7_segment_5_b, n7_segment_5_c, n7_segment_5_d, n7_segment_5_e,
       n7_segment_5_f, n7_segment_5_g, n7_segment_6_a, n7_segment_6_b, n7_segment_6_c, n7_segment_6_d,
       n7_segment_6_e, n7_segment_6_f, n7_segment_6_g, or_1_out;

  _7_segment u_7_segment_1 (
    .x1(1'b0), .x2(1'b0), .x3(mod2_1_q1), .x4(mod2_1_q2), .a(n7_segment_1_a), .b(n7_segment_1_b),
    .c(n7_segment_1_c), .d(n7_segment_1_d), .e(n7_segment_1_e), .f(n7_segment_1_f), .g(n7_segment_1_g));
  or or_1 (or_1_out, and_2_out, and_1_out);
  _7_Segment_Display u_7_segment_display_1 (
    .g(n7_segment_1_g), .f(n7_segment_1_f), .a(n7_segment_1_a), .b(n7_segment_1_b), .e(n7_segment_1_e),
    .d(n7_segment_1_d), .c(n7_segment_1_c));  // open: dp
  mod2 mod2_1 (.clock(clock_1_out), .in_2(or_1_out), .Q2(mod2_1_q2), .Q1(mod2_1_q1));
  and and_1 (and_1_out, mod1_1_q1, mod1_1_q3);
  _7_Segment_Display u_7_segment_display_2 (
    .g(n7_segment_2_g), .f(n7_segment_2_f), .a(n7_segment_2_a), .b(n7_segment_2_b), .e(n7_segment_2_e),
    .d(n7_segment_2_d), .c(n7_segment_2_c));  // open: dp
  _7_segment u_7_segment_2 (
    .x1(mod1_1_q1), .x2(mod1_1_q2), .x3(mod1_1_q3), .x4(mod1_1_q4), .a(n7_segment_2_a), .b(n7_segment_2_b),
    .c(n7_segment_2_c), .d(n7_segment_2_d), .e(n7_segment_2_e), .f(n7_segment_2_f), .g(n7_segment_2_g));
  mod1 mod1_1 (
    .clock(clock_1_out), .in_3(and_3_out), .Q4(mod1_1_q4), .Q3(mod1_1_q3), .Q2(mod1_1_q2), .Q1(mod1_1_q1),
    .reset_hour_2(and_2_out));
  and and_2 (and_2_out, mod2_1_q1, mod1_1_q2);
  and and_3 (and_3_out, mod_6_1_q2, mod_6_1_q3);
  _7_Segment_Display u_7_segment_display_3 (
    .g(n7_segment_3_g), .f(n7_segment_3_f), .a(n7_segment_3_a), .b(n7_segment_3_b), .e(n7_segment_3_e),
    .d(n7_segment_3_d), .c(n7_segment_3_c));  // open: dp
  _7_segment u_7_segment_3 (
    .x1(mod_6_1_q1), .x2(mod_6_1_q2), .x3(mod_6_1_q3), .x4(mod_6_1_q4), .a(n7_segment_3_a),
    .b(n7_segment_3_b), .c(n7_segment_3_c), .d(n7_segment_3_d), .e(n7_segment_3_e), .f(n7_segment_3_f),
    .g(n7_segment_3_g));
  mod_6 mod_6_1 (
    .clock(clock_1_out), .in_2(and_4_out), .Q4(mod_6_1_q4), .Q3(mod_6_1_q3), .Q2(mod_6_1_q2), .Q1(mod_6_1_q1));
  and and_4 (and_4_out, mod_10_1_q1, mod_10_1_q3);
  _7_segment u_7_segment_4 (
    .x1(mod_10_1_q1), .x2(mod_10_1_q2), .x3(mod_10_1_q3), .x4(mod_10_1_q4), .a(n7_segment_4_a),
    .b(n7_segment_4_b), .c(n7_segment_4_c), .d(n7_segment_4_d), .e(n7_segment_4_e), .f(n7_segment_4_f),
    .g(n7_segment_4_g));
  _7_Segment_Display u_7_segment_display_4 (
    .g(n7_segment_4_g), .f(n7_segment_4_f), .a(n7_segment_4_a), .b(n7_segment_4_b), .e(n7_segment_4_e),
    .d(n7_segment_4_d), .c(n7_segment_4_c));  // open: dp
  mod_10 mod_10_1 (
    .clock(clock_1_out), .in_2(and_5_out), .Q4(mod_10_1_q4), .Q3(mod_10_1_q3), .Q2(mod_10_1_q2),
    .Q1(mod_10_1_q1));
  and and_5 (and_5_out, mod_6_2_q2, mod_6_2_q3);
  _7_Segment_Display u_7_segment_display_5 (
    .g(n7_segment_5_g), .f(n7_segment_5_f), .a(n7_segment_5_a), .b(n7_segment_5_b), .e(n7_segment_5_e),
    .d(n7_segment_5_d), .c(n7_segment_5_c));  // open: dp
  _7_segment u_7_segment_5 (
    .x1(mod_6_2_q1), .x2(mod_6_2_q2), .x3(mod_6_2_q3), .x4(mod_6_2_q4), .a(n7_segment_5_a),
    .b(n7_segment_5_b), .c(n7_segment_5_c), .d(n7_segment_5_d), .e(n7_segment_5_e), .f(n7_segment_5_f),
    .g(n7_segment_5_g));
  mod_6 mod_6_2 (
    .clock(clock_1_out), .in_2(and_6_out), .Q4(mod_6_2_q4), .Q3(mod_6_2_q3), .Q2(mod_6_2_q2), .Q1(mod_6_2_q1));
  and and_6 (and_6_out, mod_10_2_q3, mod_10_2_q1);
  _7_Segment_Display u_7_segment_display_6 (
    .g(n7_segment_6_g), .f(n7_segment_6_f), .a(n7_segment_6_a), .b(n7_segment_6_b), .e(n7_segment_6_e),
    .d(n7_segment_6_d), .c(n7_segment_6_c));  // open: dp
  _7_segment u_7_segment_6 (
    .x1(mod_10_2_q1), .x2(mod_10_2_q2), .x3(mod_10_2_q3), .x4(mod_10_2_q4), .a(n7_segment_6_a),
    .b(n7_segment_6_b), .c(n7_segment_6_c), .d(n7_segment_6_d), .e(n7_segment_6_e), .f(n7_segment_6_f),
    .g(n7_segment_6_g));
  mod_10 mod_10_2 (
    .clock(clock_1_out), .in_2(1'b1), .Q4(mod_10_2_q4), .Q3(mod_10_2_q3), .Q2(mod_10_2_q2), .Q1(mod_10_2_q1));
  Clock clock_1 (.out(clock_1_out));
endmodule

module mod_10 (
  input  clock,
  input  in_2,
  output Q4,
  output Q3,
  output Q2,
  output Q1
);

  wire and_1_out, and_2_out, and_3_out, and_4_out;

  J_K_Flip_Flop j_k_ff_1 (.J(1'b1), .clk(and_1_out), .K(1'b1), .Q(Q4), .reset(and_4_out));  // open: Qn, preset, en
  and and_1 (and_1_out, clock, in_2);
  and and_2 (and_2_out, Q4, Q3);
  J_K_Flip_Flop j_k_ff_2 (.J(Q4), .clk(and_1_out), .K(Q4), .Q(Q3), .reset(and_4_out));  // open: Qn, preset, en
  J_K_Flip_Flop j_k_ff_3 (
    .J(and_2_out), .clk(and_1_out), .K(and_2_out), .Q(Q2), .reset(and_4_out));  // open: Qn, preset, en
  and and_3 (and_3_out, and_2_out, Q2);
  J_K_Flip_Flop j_k_ff_4 (
    .J(and_3_out), .clk(and_1_out), .K(and_3_out), .Q(Q1), .reset(and_4_out));  // open: Qn, preset, en
  and and_4 (and_4_out, Q1, Q3);
endmodule

module _7_segment (
  input  x1,
  input  x2,
  input  x3,
  input  x4,
  output a,
  output b,
  output c,
  output d,
  output e,
  output f,
  output g
);

  wire and_1_out, and_2_out, and_3_out, and_4_out, and_5_out, and_6_out, and_7_out, and_8_out, and_9_out,
       and_10_out, and_11_out, and_12_out, and_13_out, and_14_out, and_15_out, and_16_out, not_1_out,
       not_2_out, not_3_out, not_4_out, not_5_out, not_6_out, not_7_out, not_8_out, not_9_out, not_10_out,
       not_11_out, not_12_out, not_13_out, not_14_out, not_15_out, not_16_out, not_17_out, not_18_out,
       not_19_out, not_20_out, not_21_out;

  not not_1 (not_1_out, x2);
  and and_1 (and_1_out, not_1_out, not_2_out);
  not not_2 (not_2_out, x4);
  and and_2 (and_2_out, x2, x4);
  not not_3 (not_3_out, x2);
  not not_4 (not_4_out, x3);
  and and_3 (and_3_out, not_4_out, not_5_out);
  not not_5 (not_5_out, x4);
  and and_4 (and_4_out, x3, x4);
  not not_6 (not_6_out, x3);
  or or_1 (c, not_6_out, x4, x2);
  not not_7 (not_7_out, x2);
  and and_5 (and_5_out, not_7_out, not_8_out);
  not not_8 (not_8_out, x4);
  not not_9 (not_9_out, x2);
  and and_6 (and_6_out, not_9_out, x3);
  and and_7 (and_7_out, x3, not_10_out);
  not not_10 (not_10_out, x4);
  not not_11 (not_11_out, x3);
  and and_8 (and_8_out, x2, not_11_out, x4);
  not not_12 (not_12_out, x2);
  and and_9 (and_9_out, not_12_out, not_13_out);
  not not_13 (not_13_out, x4);
  and and_10 (and_10_out, x3, not_14_out);
  not not_14 (not_14_out, x4);
  not not_15 (not_15_out, x3);
  and and_11 (and_11_out, not_15_out, not_16_out);
  not not_16 (not_16_out, x4);
  and and_12 (and_12_out, x2, not_17_out);
  not not_17 (not_17_out, x3);
  and and_13 (and_13_out, x2, not_18_out);
  not not_18 (not_18_out, x4);
  not not_19 (not_19_out, x2);
  and and_14 (and_14_out, not_19_out, x3);
  and and_15 (and_15_out, x2, not_20_out);
  not not_20 (not_20_out, x3);
  and and_16 (and_16_out, x2, not_21_out);
  not not_21 (not_21_out, x4);
  or or_2 (a, and_1_out, x3, and_2_out, x1);
  or or_3 (b, not_3_out, and_3_out, and_4_out);
  or or_4 (d, and_5_out, and_6_out, and_7_out, and_8_out, x1);
  or or_5 (e, and_9_out, and_10_out);
  or or_6 (f, and_11_out, and_12_out, and_13_out, x1);
  or or_7 (g, and_14_out, and_15_out, and_16_out, x1);
endmodule

module mod_6 (
  input  clock,
  input  in_2,
  output Q4,
  output Q3,
  output Q2,
  output Q1
);

  wire and_1_out, and_2_out, and_3_out, and_4_out;

  J_K_Flip_Flop j_k_ff_1 (.J(1'b1), .clk(and_1_out), .K(1'b1), .Q(Q4), .reset(and_4_out));  // open: Qn, preset, en
  and and_1 (and_1_out, clock, in_2);
  and and_2 (and_2_out, Q4, Q3);
  J_K_Flip_Flop j_k_ff_2 (.J(Q4), .clk(and_1_out), .K(Q4), .Q(Q3), .reset(and_4_out));  // open: Qn, preset, en
  J_K_Flip_Flop j_k_ff_3 (
    .J(and_2_out), .clk(and_1_out), .K(and_2_out), .Q(Q2), .reset(and_4_out));  // open: Qn, preset, en
  and and_3 (and_3_out, and_2_out, Q2);
  J_K_Flip_Flop j_k_ff_4 (
    .J(and_3_out), .clk(and_1_out), .K(and_3_out), .Q(Q1), .reset(and_4_out));  // open: Qn, preset, en
  and and_4 (and_4_out, Q2, Q3);
endmodule

module mod2 (
  input  clock,
  input  in_2,
  output Q2,
  output Q1
);

  wire and_1_out, and_2_out;

  and and_1 (and_1_out, clock, in_2);
  J_K_Flip_Flop j_k_ff_1 (.J(1'b1), .clk(and_1_out), .K(1'b1), .Q(Q2), .reset(and_2_out));  // open: Qn, preset, en
  J_K_Flip_Flop j_k_ff_2 (.J(Q2), .clk(and_1_out), .K(Q2), .Q(Q1), .reset(and_2_out));  // open: Qn, preset, en
  and and_2 (and_2_out, Q2, Q1);
endmodule

module mod1 (
  input  reset_hour_2,
  input  clock,
  input  in_3,
  output Q4,
  output Q3,
  output Q2,
  output Q1
);

  wire and_1_out, and_2_out, and_3_out, and_4_out, or_1_out;

  J_K_Flip_Flop j_k_ff_1 (.J(1'b1), .clk(and_1_out), .K(1'b1), .Q(Q4), .reset(or_1_out));  // open: Qn, preset, en
  and and_1 (and_1_out, clock, in_3);
  J_K_Flip_Flop j_k_ff_2 (.J(Q4), .clk(and_1_out), .K(Q4), .Q(Q3), .reset(or_1_out));  // open: Qn, preset, en
  and and_2 (and_2_out, Q4, Q3);
  and and_3 (and_3_out, and_2_out, Q2);
  J_K_Flip_Flop j_k_ff_3 (
    .J(and_2_out), .clk(and_1_out), .K(and_2_out), .Q(Q2), .reset(or_1_out));  // open: Qn, preset, en
  J_K_Flip_Flop j_k_ff_4 (
    .J(and_3_out), .clk(and_1_out), .K(and_3_out), .Q(Q1), .reset(or_1_out));  // open: Qn, preset, en
  or or_1 (or_1_out, and_4_out, reset_hour_2);
  and and_4 (and_4_out, Q3, Q1);
endmodule
