// Logisim project second-minutes-hours-counter.circ as structural Verilog: 3 circuits, main circuit main
module main (
);

  wire and_1_out, and_2_out, and_3_out, and_4_out, and_5_out, n3_bit_counter_1_q0, n3_bit_counter_1_q1,
       n3_bit_counter_1_q2, n3_bit_counter_2_q0, n3_bit_counter_2_q1, n3_bit_counter_2_q2,
       n4_bit_counter_1_q0, n4_bit_counter_1_q1, n4_bit_counter_1_q2, n4_bit_counter_1_q3,
       n4_bit_counter_2_q0, n4_bit_counter_2_q1, n4_bit_counter_2_q2, n4_bit_counter_2_q3,
       n4_bit_counter_3_q0, n4_bit_counter_3_q1, n4_bit_counter_3_q2, n4_bit_counter_3_q3,
       n4_bit_counter_4_q0, n4_bit_counter_4_q1, n4_bit_counter_4_q2, n4_bit_counter_4_q3, undriven,
       undriven_2, undriven_3, undriven_4, undriven_5, undriven_6, undriven_7, undriven_8, undriven_9,
       undriven_10, undriven_11, undriven_12, undriven_13, undriven_14, undriven_15, undriven_16,
       undriven_17, undriven_18, undriven_19, undriven_20, undriven_21, undriven_22, undriven_23, undriven_24;

  _4_bit_counter u_4_bit_counter_1 (
    .clk(undriven_24), .Q0(n4_bit_counter_1_q0), .Q1(n4_bit_counter_1_q1), .Q2(n4_bit_counter_1_q2),
    .Q3(n4_bit_counter_1_q3), .enable(undriven_17), .D0(undriven_18), .D1(undriven_23), .D2(undriven_19),
    .D3(undriven_16), .load(and_1_out));
  _3_bit_counter u_3_bit_counter_1 (
    .clk(undriven_24), .Q0(n3_bit_counter_1_q0), .Q1(n3_bit_counter_1_q1), .Q2(n3_bit_counter_1_q2),
    .enable(and_1_out), .D0(undriven_20), .D1(undriven_21), .D2(undriven_22), .load(and_2_out));
  _4_bit_counter u_4_bit_counter_2 (
    .clk(undriven_24), .Q0(n4_bit_counter_2_q0), .Q1(n4_bit_counter_2_q1), .Q2(n4_bit_counter_2_q2),
    .Q3(n4_bit_counter_2_q3), .enable(and_2_out), .D0(undriven), .D1(undriven_2), .D2(undriven_3),
    .D3(undriven_4), .load(and_3_out));
  _3_bit_counter u_3_bit_counter_2 (
    .clk(undriven_24), .Q0(n3_bit_counter_2_q0), .Q1(n3_bit_counter_2_q1), .Q2(n3_bit_counter_2_q2),
    .enable(and_3_out), .D0(undriven_5), .D1(undriven_6), .D2(undriven_7), .load(and_4_out));
  _4_bit_counter u_4_bit_counter_3 (
    .clk(undriven_24), .Q0(n4_bit_counter_3_q0), .Q1(n4_bit_counter_3_q1), .Q2(n4_bit_counter_3_q2),
    .Q3(n4_bit_counter_3_q3), .enable(and_4_out), .D0(undriven_8), .D1(undriven_9), .D2(undriven_10),
    .D3(undriven_11), .load(and_5_out));
  _4_bit_counter u_4_bit_counter_4 (
    .clk(undriven_24), .Q0(n4_bit_counter_4_q0), .Q1(n4_bit_counter_4_q1), .Q2(n4_bit_counter_4_q2),
    .Q3(n4_bit_counter_4_q3), .enable(and_5_out), .D0(undriven_12), .D1(undriven_13), .D2(undriven_14),
    .D3(undriven_15));  // open: load
  and and_1 (and_1_out, n4_bit_counter_1_q0, n4_bit_counter_1_q3);
  and and_2 (and_2_out, n3_bit_counter_1_q2, and_1_out, n3_bit_counter_1_q0);
  and and_3 (and_3_out, n4_bit_counter_2_q0, and_2_out, n4_bit_counter_2_q3);
  and and_4 (and_4_out, n3_bit_counter_2_q0, n3_bit_counter_2_q2, and_3_out);
  and and_5 (and_5_out, n4_bit_counter_3_q0, and_4_out, n4_bit_counter_3_q3);
  // AND_Gate and_6 has open pins: in0=n4_bit_counter_4_q3, in1=and_5_out, in2=n4_bit_counter_4_q0, out=open
endmodule

module _4_bit_counter (
  input  clk,
  input  D0,
  input  enable,
  input  D3,
  input  D1,
  input  D2,
  input  load,
  output Q2,
  output Q1,
  output Q3,
  output Q0
);

  wire and_1_out, and_2_out, and_3_out, multiplexer_1_out, multiplexer_2_out, multiplexer_3_out,
       multiplexer_4_out, xor_1_out, xor_2_out, xor_3_out, xor_4_out;

  xor xor_1 (xor_1_out, Q0, enable);
  Multiplexer #(.enable("false")) multiplexer_1 (.in0(xor_1_out), .in1(D0), .out(multiplexer_1_out), .sel(load));
  D_Flip_Flop d_ff_1 (.clk(clk), .D(multiplexer_1_out), .Q(Q0));  // open: Qn, preset, en, reset
  and and_1 (and_1_out, Q0, enable);
  xor xor_2 (xor_2_out, Q1, and_1_out);
  Multiplexer #(.enable("false")) multiplexer_2 (.in0(xor_2_out), .in1(D1), .out(multiplexer_2_out), .sel(load));
  and and_2 (and_2_out, Q1, and_1_out);
  D_Flip_Flop d_ff_2 (.clk(clk), .D(multiplexer_2_out), .Q(Q1));  // open: Qn, preset, en, reset
  xor xor_3 (xor_3_out, Q2, and_2_out);
  Multiplexer #(.enable("false")) multiplexer_3 (.in0(xor_3_out), .in1(D2), .out(multiplexer_3_out), .sel(load));
  and and_3 (and_3_out, Q2, and_2_out);
  D_Flip_Flop d_ff_3 (.clk(clk), .D(multiplexer_3_out), .Q(Q2));  // open: Qn, preset, en, reset
  xor xor_4 (xor_4_out, Q3, and_3_out);
  Multiplexer #(.enable("false")) multiplexer_4 (.in0(xor_4_out), .in1(D3), .out(multiplexer_4_out), .sel(load));
  D_Flip_Flop d_ff_4 (.clk(clk), .D(multiplexer_4_out), .Q(Q3));  // open: Qn, preset, en, reset
endmodule

module _3_bit_counter (
  input  clk,
  input  D0,
  input  enable,
  input  D1,
  input  D2,
  input  load,
  output Q2,
  output Q1,
  output Q0
);

  wire and_1_out, and_2_out, multiplexer_1_out, multiplexer_2_out, multiplexer_3_out, xor_1_out, xor_2_out,
       xor_3_out;

  xor xor_1 (xor_1_out, Q0, enable);
  Multiplexer #(.enable("false")) multiplexer_1 (.in0(xor_1_out), .in1(D0), .out(multiplexer_1_out), .sel(load));
  D_Flip_Flop d_ff_1 (.clk(clk), .D(multiplexer_1_out), .Q(Q0));  // open: Qn, preset, en, reset
  and and_1 (and_1_out, Q0, enable);
  xor xor_2 (xor_2_out, Q1, and_1_out);
  Multiplexer #(.enable("false")) multiplexer_2 (.in0(xor_2_out), .in1(D1), .out(multiplexer_2_out), .sel(load));
  and and_2 (and_2_out, Q1, and_1_out);
  D_Flip_Flop d_ff_2 (.clk(clk), .D(multiplexer_2_out), .Q(Q1));  // open: Qn, preset, en, reset
  xor xor_3 (xor_3_out, Q2, and_2_out);
  Multiplexer #(.enable("false")) multiplexer_3 (.in0(xor_3_out), .in1(D2), .out(multiplexer_3_out), .sel(load));
  D_Flip_Flop d_ff_3 (.clk(clk), .D(multiplexer_3_out), .Q(Q2));  // open: Qn, preset, en, reset
endmodule
